// Logisim project 23071005-task2.circ as structural Verilog: 7 circuits, main circuit 23071005+add1
module _23071005_add1 (
  input  A_in,
  input  B_in,
  input  C_in,
  output Out_1,
  output Out_2
);

  wire and_1_out, and_2_out, xor_1_out;

  xor xor_1 (xor_1_out, A_in, B_in);
  and and_1 (and_1_out, B_in, A_in);
  and and_2 (and_2_out, xor_1_out, C_in);
  xor xor_2 (Out_1, xor_1_out, C_in);
  xor xor_3 (Out_2, and_1_out, and_2_out);
endmodule

module _23071005_add4 (
  input  Carry_bit_in,
  input  [3:0] in_2,
  input  [3:0] in_3,
  output [3:0] Out,
  output Carry_bit_out
);

  wire n23071005_add1_1_out_2, n23071005_add1_2_out_2, n23071005_add1_3_out_2;

  _23071005_add1 u_23071005_add1_1 (
    .A_in(in_2[0]), .B_in(in_3[0]), .C_in(Carry_bit_in), .Out_1(Out[0]), .Out_2(n23071005_add1_1_out_2));
  _23071005_add1 u_23071005_add1_2 (
    .A_in(in_2[1]), .B_in(in_3[1]), .C_in(n23071005_add1_1_out_2), .Out_1(Out[1]),
    .Out_2(n23071005_add1_2_out_2));
  _23071005_add1 u_23071005_add1_3 (
    .A_in(in_2[2]), .B_in(in_3[2]), .C_in(n23071005_add1_2_out_2), .Out_1(Out[2]),
    .Out_2(n23071005_add1_3_out_2));
  _23071005_add1 u_23071005_add1_4 (
    .A_in(in_2[3]), .B_in(in_3[3]), .C_in(n23071005_add1_3_out_2), .Out_1(Out[3]), .Out_2(Carry_bit_out));
endmodule

module _23071005_add16 (
  input  Carry_bit_in,
  input  [15:0] in_2,
  input  [15:0] in_3,
  output [15:0] Out,
  output Carry_bit_out
);

  wire n23071005_add4_1_carry_bit_out, n23071005_add4_2_carry_bit_out, n23071005_add4_3_carry_bit_out;

  _23071005_add4 u_23071005_add4_1 (
    .Carry_bit_in(Carry_bit_in), .in_2(in_2[3:0]), .in_3(in_3[3:0]), .Out(Out[3:0]),
    .Carry_bit_out(n23071005_add4_1_carry_bit_out));
  _23071005_add4 u_23071005_add4_2 (
    .Carry_bit_in(n23071005_add4_1_carry_bit_out), .in_2(in_2[7:4]), .in_3(in_3[7:4]), .Out(Out[7:4]),
    .Carry_bit_out(n23071005_add4_2_carry_bit_out));
  _23071005_add4 u_23071005_add4_3 (
    .Carry_bit_in(n23071005_add4_2_carry_bit_out), .in_2(in_2[11:8]), .in_3(in_3[11:8]), .Out(Out[11:8]),
    .Carry_bit_out(n23071005_add4_3_carry_bit_out));
  _23071005_add4 u_23071005_add4_4 (
    .Carry_bit_in(n23071005_add4_3_carry_bit_out), .in_2(in_2[15:12]), .in_3(in_3[15:12]), .Out(Out[15:12]),
    .Carry_bit_out(Carry_bit_out));
endmodule

module _23071005_add32 (
  input  Carry_bit_in,
  input  [31:0] in_2,
  input  [31:0] in_3,
  output [31:0] Out,
  output Carry_bit_out
);

  wire n23071005_add16_1_carry_bit_out;

  _23071005_add16 u_23071005_add16_1 (
    .Carry_bit_in(Carry_bit_in), .in_2(in_2[15:0]), .in_3(in_3[15:0]), .Out(Out[15:0]),
    .Carry_bit_out(n23071005_add16_1_carry_bit_out));
  _23071005_add16 u_23071005_add16_2 (
    .Carry_bit_in(n23071005_add16_1_carry_bit_out), .in_2(in_2[31:16]), .in_3(in_3[31:16]), .Out(Out[31:16]),
    .Carry_bit_out(Carry_bit_out));
endmodule

module _23071005_sub32 (
  input  [31:0] A_in,
  input  [31:0] B_in,
  output [31:0] sub_out,
  output carry_bit_out
);

  wire [31:0] not_1_out;

  assign not_1_out = ~B_in;  // NOT_Gate not_1, 32 bits wide
  _23071005_add32 u_23071005_add32_1 (
    .Carry_bit_in(1'b1), .in_2(A_in), .in_3(not_1_out), .Out(sub_out), .Carry_bit_out(carry_bit_out));
endmodule

module _23071005_4modeALU (
  input  [1:0] ALU_sel,
  input  [31:0] A_in,
  input  [31:0] B_in,
  output [31:0] Out
);

  wire [31:0] and_1_out, n23071005_add32_1_out, n23071005_sub32_1_sub_out, or_1_out;

  _23071005_add32 u_23071005_add32_1 (
    .Carry_bit_in(1'b0), .in_2(A_in), .in_3(B_in), .Out(n23071005_add32_1_out));  // open: Carry_bit_out
  _23071005_sub32 u_23071005_sub32_1 (
    .A_in(A_in), .B_in(B_in), .sub_out(n23071005_sub32_1_sub_out));  // open: carry_bit_out
  assign and_1_out = A_in & B_in;  // AND_Gate and_1, 32 bits wide
  assign or_1_out = B_in | A_in;  // OR_Gate or_1, 32 bits wide
  Multiplexer #(.select(2), .width(32)) multiplexer_1 (
    .in0(n23071005_add32_1_out), .in1(n23071005_sub32_1_sub_out), .in2(and_1_out), .in3(or_1_out), .out(Out),
    .sel(ALU_sel), .en(1'b1));
endmodule

module ALU_23071005 (
  input  [1:0] ALU_sel,
  input  [31:0] A_in,
  input  [31:0] B_in,
  output zero,
  output [31:0] ALU_out
);

  wire or_1_out;

  _23071005_4modeALU u_23071005_4modealu_1 (.ALU_sel(ALU_sel), .A_in(A_in), .B_in(B_in), .Out(ALU_out));
  or or_1 (or_1_out, ALU_out[15], ALU_out[0], ALU_out[1], ALU_out[2], ALU_out[3], ALU_out[4], ALU_out[5], ALU_out[6], ALU_out[7], ALU_out[8], ALU_out[9], ALU_out[10], ALU_out[11], ALU_out[12], ALU_out[13], ALU_out[14], ALU_out[16], ALU_out[17], ALU_out[18], ALU_out[19], ALU_out[20], ALU_out[21], ALU_out[22], ALU_out[23], ALU_out[24], ALU_out[25], ALU_out[26], ALU_out[27], ALU_out[28], ALU_out[29], ALU_out[30], ALU_out[31]);
  not not_1 (zero, or_1_out);
endmodule
