// Logisim project 23071005-task3.circ as structural Verilog: 1 circuit, main circuit num-23071005
module num_23071005 (
  input  [1:0] Extsel,
  input  [15:0] Imm16,
  output [31:0] ExtImm32
);

  Multiplexer #(.select(2), .width(32), .enable("false")) multiplexer_1 (
    .in0({{16{1'b0}}, Imm16}), .in1({{17{Imm16[15]}}, Imm16[14:0]}), .in2({Imm16, {16{1'b0}}}),
    .out(ExtImm32), .sel(Extsel));  // open: in3
endmodule
