// Logisim project 23071005-task4.circ as structural Verilog: 1 circuit, main circuit Mdec-23071005
module Mdec_23071005 (
  input  [5:0] opcode,
  input  [5:0] funct,
  output beq,
  output sw,
  output lw,
  output lui,
  output ori,
  output subu,
  output addu
);

  wire comparator_6_eq, comparator_7_eq, comparator_8_eq;

  Comparator #(.width(6)) comparator_1 (.a(opcode), .b(6'b000100), .eq(beq));  // open: gt, lt
  Comparator #(.width(6)) comparator_2 (.a(opcode), .b(6'b101011), .eq(sw));  // open: gt, lt
  Comparator #(.width(6)) comparator_3 (.a(opcode), .b(6'b100011), .eq(lw));  // open: gt, lt
  Comparator #(.width(6)) comparator_4 (.a(opcode), .b(6'b001111), .eq(lui));  // open: gt, lt
  Comparator #(.width(6)) comparator_5 (.a(opcode), .b(6'b001101), .eq(ori));  // open: gt, lt
  Comparator #(.width(6)) comparator_6 (.a(opcode), .b({6{1'b0}}), .eq(comparator_6_eq));  // open: gt, lt
  Comparator #(.width(6)) comparator_7 (.a(funct), .b(6'b100001), .eq(comparator_7_eq));  // open: gt, lt
  Comparator #(.width(6)) comparator_8 (.a(funct), .b(6'b100011), .eq(comparator_8_eq));  // open: gt, lt
  and and_1 (addu, comparator_6_eq, comparator_7_eq);
  and and_2 (subu, comparator_6_eq, comparator_8_eq);
endmodule
