// Logisim project 23071005-task5.circ as structural Verilog: 1 circuit, main circuit Mcod-23071005
module Mcod_23071005 (
  input  [6:0] _6bit_in,
  input  zero,
  output PC_sel,
  output [1:0] EXT_sel,
  output [1:0] ALU_sel,
  output B_sel
);

  wire or_1_out;

  and and_1 (PC_sel, _6bit_in[0], zero);
  or or_1 (or_1_out, _6bit_in[6], _6bit_in[5], _6bit_in[0]);
  or or_2 (ALU_sel[0], _6bit_in[5], _6bit_in[4], _6bit_in[0]);
  or or_3 (EXT_sel[0], _6bit_in[2], _6bit_in[1]);
  not not_1 (B_sel, or_1_out);

  assign ALU_sel[1] = _6bit_in[4];
  assign EXT_sel[1] = _6bit_in[3];
endmodule
