// Logisim project 23071005-task6.circ as structural Verilog: 1 circuit, main circuit 23071005-ALL
module _23071005_ALL (
  input  [31:0] A_in,
  input  [31:0] B_in,
  input  [15:0] Imm16,
  input  [5:0] opcode,
  input  [5:0] funct,
  output [31:0] ALU_out,
  output PC_sel
);

  wire ALU_23071005_zero, Mcod_23071005_b_sel;
  wire [1:0] Mcod_23071005_alu_sel, Mcod_23071005_ext_sel;
  wire [6:0] Mdec_23071005_beq;
  wire [31:0] multiplexer_1_out, num_23071005_extimm32;

  num_23071005 num_23071005 (.Extsel(Mcod_23071005_ext_sel), .Imm16(Imm16), .ExtImm32(num_23071005_extimm32));
  Mdec_23071005 Mdec_23071005 (
    .opcode(opcode), .funct(funct), .beq(Mdec_23071005_beq[0]), .sw(Mdec_23071005_beq[1]),
    .lw(Mdec_23071005_beq[2]), .lui(Mdec_23071005_beq[3]), .ori(Mdec_23071005_beq[4]),
    .subu(Mdec_23071005_beq[5]), .addu(Mdec_23071005_beq[6]));
  Multiplexer #(.width(32), .enable("false")) multiplexer_1 (
    .in0(B_in), .in1(num_23071005_extimm32), .out(multiplexer_1_out), .sel(Mcod_23071005_b_sel));
  Mcod_23071005 Mcod_23071005 (
    ._6bit_in(Mdec_23071005_beq), .zero(ALU_23071005_zero), .PC_sel(PC_sel), .EXT_sel(Mcod_23071005_ext_sel),
    .ALU_sel(Mcod_23071005_alu_sel), .B_sel(Mcod_23071005_b_sel));
  ALU_23071005 ALU_23071005 (
    .ALU_sel(Mcod_23071005_alu_sel), .A_in(A_in), .B_in(multiplexer_1_out), .zero(ALU_23071005_zero),
    .ALU_out(ALU_out));
endmodule
