// Logisim project 23071005-task7.circ as structural Verilog: 1 circuit, main circuit laundry_machine
module laundry_machine (
  input  water_level_high,
  input  lid_closed,
  input  pressed_run
);

  wire and_1_out, and_2_out, and_3_out, comparator_1_eq, comparator_2_eq, comparator_3_eq, comparator_4_eq,
       comparator_5_eq, connect_frequency_divider_out, nand_1_out, not_1_out, not_2_out, not_3_out, or_1_out,
       or_2_out, reset_out;
  wire [2:0] counter_1_q;

  Clock connect_frequency_divider (.out(connect_frequency_divider_out));
  Button reset (.out(reset_out));
  nand nand_1 (nand_1_out, water_level_high, lid_closed);
  Counter #(.width(3), .max('h4)) counter_1 (
    .Q(counter_1_q), .clk(connect_frequency_divider_out), .clr(or_1_out));  // open: load, D, count, carry
  or or_1 (or_1_out, not_1_out, or_2_out);
  not not_1 (not_1_out, pressed_run);
  or or_2 (or_2_out, reset_out, comparator_1_eq, and_1_out);
  and and_1 (and_1_out, nand_1_out, pressed_run);
  Comparator #(.width(3)) comparator_1 (.a(counter_1_q), .b(3'b100), .eq(comparator_1_eq));  // open: gt, lt
  Comparator #(.width(3)) comparator_2 (.a(counter_1_q), .b(3'b011), .eq(comparator_2_eq));  // open: gt, lt
  Comparator #(.width(3)) comparator_3 (.a(counter_1_q), .b(3'b010), .eq(comparator_3_eq));  // open: gt, lt
  Comparator #(.width(3)) comparator_4 (.a(counter_1_q), .b(3'b001), .eq(comparator_4_eq));  // open: gt, lt
  Comparator #(.width(3)) comparator_5 (.a(counter_1_q), .b(3'b000), .eq(comparator_5_eq));  // open: gt, lt
  not not_2 (not_2_out, pressed_run);
  not not_3 (not_3_out, and_1_out);
  LED done (.in(comparator_2_eq));
  LED drying (.in(comparator_3_eq));
  LED rinsing (.in(comparator_4_eq));
  LED washing (.in(and_2_out));
  and and_2 (and_2_out, comparator_5_eq, not_3_out, pressed_run);
  LED plz_press_run (.in(and_3_out));
  and and_3 (and_3_out, comparator_5_eq, not_2_out);
  LED ERROR (.in(and_1_out));
endmodule
