// Logisim project task1.circ as structural Verilog: 3 circuits, main circuit 大作业逻辑图
// 23071005_label
module \大作业逻辑图  (
  input  [3:0] \ＩＮ ,
  input  [1:0] S,
  output [3:0] \ＯＵＴ ,
  output FLAG
);

  wire decoder_1_out5, decoder_1_out6, decoder_1_out7, decoder_1_out8, decoder_1_out9, decoder_1_out10,
       decoder_1_out11, decoder_1_out12, decoder_1_out13, decoder_1_out14, decoder_1_out15, not_1_out,
       or_2_out;
  wire [2:0] xor_1_out;
  wire [3:0] adder_1_out, adder_2_out, multiplexer_1_out, multiplexer_2_out;

  Decoder #(.select(4), .enable("false")) decoder_1 (
    .out5(decoder_1_out5), .out6(decoder_1_out6), .out7(decoder_1_out7), .out8(decoder_1_out8),
    .out9(decoder_1_out9), .out10(decoder_1_out10), .out11(decoder_1_out11), .out12(decoder_1_out12),
    .out13(decoder_1_out13), .out14(decoder_1_out14), .out15(decoder_1_out15), .sel(\ＩＮ ));  // open: out0, out1, out2, out3, out4
  or or_1 (FLAG, decoder_1_out10, decoder_1_out11, decoder_1_out12, decoder_1_out13, decoder_1_out14, decoder_1_out15);
  Adder #(.width(4)) adder_1 (.a(\ＩＮ ), .b(4'b0011), .out(adder_1_out));  // open: cin, cout
  Multiplexer #(.width(4), .enable("false")) multiplexer_1 (
    .in0(4'b0000), .in1(4'b0110), .out(multiplexer_1_out), .sel(or_2_out));
  or or_2 (or_2_out, decoder_1_out5, decoder_1_out6, decoder_1_out7, decoder_1_out8, decoder_1_out9);
  Adder #(.width(4)) adder_2 (.a(\ＩＮ ), .b(multiplexer_1_out), .out(adder_2_out));  // open: cin, cout
  not not_1 (not_1_out, FLAG);
  xor xor_1 (xor_1_out[0], \ＩＮ [0], \ＩＮ [1]);
  xor xor_2 (xor_1_out[1], \ＩＮ [1], \ＩＮ [2]);
  xor xor_3 (xor_1_out[2], \ＩＮ [2], \ＩＮ [3]);
  Multiplexer #(.width(4), .enable("false")) multiplexer_2 (
    .in0({\ＩＮ [3], xor_1_out}), .in1(4'b1000), .out(multiplexer_2_out), .sel(decoder_1_out9));
  Multiplexer #(.select(2), .width(4), .disabled(0)) multiplexer_3 (
    .in0(adder_1_out), .in1(adder_2_out), .in2(multiplexer_2_out), .in3(4'b0000), .out(\ＯＵＴ ), .sel(S),
    .en(not_1_out));
endmodule

module \应用测试  (
  input  [3:0] \ＡＢＣＤ ,
  input  [1:0] \ＳＥＬ ,
  output [3:0] \ＯＵＴ３_０ ,
  output \ＦＬＡＧ 
);

  \大作业逻辑图  \u_大作业逻辑图_1  (.\ＩＮ (\ＡＢＣＤ ), .S(\ＳＥＬ ), .\ＯＵＴ (\ＯＵＴ３_０ ), .FLAG(\ＦＬＡＧ ));
endmodule

module tt (
  input  [7:0] in_1,
  input  in_2,
  input  in_3,
  input  in_4,
  input  in_5,
  input  [1:0] in_6,
  input  in_7,
  input  [2:0] in_8,
  input  in_9,
  input  in_10,
  input  in_11,
  input  in_12,
  input  in_13,
  input  in_14,
  input  in_15,
  input  [7:0] in_16,
  input  in_17,
  input  in_18,
  input  [7:0] in_19,
  input  in_20,
  input  in_21,
  input  in_22,
  output out_23,
  output out_24,
  output out_25,
  output [2:0] out_26,
  output out_27,
  output [15:0] out_28,
  output out_29,
  output [7:0] out_30,
  output [2:0] out_31,
  output [7:0] out_32,
  output out_33
);

  BitSelector bitselector_1 (.in(in_1), .out(out_25), .sel(in_8));
  D_Flip_Flop d_ff_1 ();  // open: clk, D, Q, Qn, preset, en, reset
  Multiplier multiplier_1 ();  // open: a, b, out, cin, cout
  Register register_1 (.D(in_16), .en(in_20), .Q(out_32), .clk(in_21), .clr(in_22));
  Priority_Encoder priority_encoder_1 (
    .in0(in_2), .in1(in_4), .in2(in_5), .in3(in_7), .in4(in_9), .in5(in_10), .in6(in_11), .in7(in_12),
    .out(out_26), .en_in(in_13), .gs(out_27), .en_out(out_24));
  Negator negator_1 (.in(in_16), .out(out_30));
  BitFinder bitfinder_1 (.in(in_19), .index(out_31), .found(out_33));
  Decoder #(.select(2)) decoder_1 (.out0(out_23), .sel(in_6), .en(in_3));  // open: out1, out2, out3
  assign out_28 = {{8{1'b0}}, in_16};  // Bit_Extender bit_extender_1
  Multiplexer multiplexer_1 (.in0(in_18), .in1(in_17), .out(out_29), .sel(in_14), .en(in_15));
endmodule
