// Logisim project grandprojectLC.circ as structural Verilog: 7 circuits, main circuit main
module main (
);

  wire ALUSrc, and_1_out, Branch, Branch_Taken_OR_Jump, clk_out, JumpCtrl, MemtoReg, MemWrite, RegDst,
       RegWrite, reset_out, Zero;
  wire [1:0] ALUOp, ExtensionControl;
  wire [4:0] WriteReg;
  wire [5:0] funct, OpCode;
  wire [15:6] Immediate;
  wire [25:16] Jump;
  wire [31:0] adder_1_out, ALU_res, Branch_Target_Address, CurrentPC, DM_23071005_readdata,
       EXT_23071005_extendedimmediate, multiplexer_3_out, ReadData1, ReadData2, S_J_addr, shifter_1_out,
       WriteData;

  Clock #(.highDuration(1), .lowDuration(1)) clk (.out(clk_out));
  Button reset (.out(reset_out));
  // Probe on CurrentPC
  // Probe on OpCode
  // Probe on {Immediate, funct}
  // Probe on funct
  // Probe on {OpCode, Jump, Immediate, funct}
  and and_1 (and_1_out, Branch, Zero);
  IFU IFU_23071005 (
    .PC_clk(clk_out), .PC_clr(reset_out), .S_J_addr(S_J_addr), .command_sel(Branch_Taken_OR_Jump),
    .IM_data({OpCode, Jump, Immediate, funct}), .CurrentPC(CurrentPC));
  GPR GPR_23071005 (
    .ReadReg1(Jump[25:21]), .ReadReg2(Jump[20:16]), .clk(clk_out), .clr(reset_out), .D(WriteData),
    .RegWrite(RegWrite), .WriteReg(WriteReg), .ReadData1(ReadData1), .ReadData2(ReadData2));
  DM DM_23071005 (
    .Address(ALU_res), .WriteData(ReadData2), .MemWrite(MemWrite), .DM_clk(clk_out), .DM_reset(reset_out),
    .ReadData(DM_23071005_readdata));
  Multiplexer #(.select(1), .width(32), .disabled("Z"), .enable("false")) multiplexer_1 (
    .in0(ALU_res), .in1(DM_23071005_readdata), .out(WriteData), .sel(MemtoReg));
  or or_1 (Branch_Taken_OR_Jump, and_1_out, JumpCtrl);
  EXT EXT_23071005 (
    .Immediate16({Immediate, funct}), .ExtensionControl(ExtensionControl),
    .ExtendedImmediate(EXT_23071005_extendedimmediate));
  Controller Controller_23071005 (
    .OpCode_31__26(OpCode), .Funct_5__0(funct), .RegWrite(RegWrite), .MemWrite(MemWrite), .ALUSrc(ALUSrc),
    .MemtoReg(MemtoReg), .RegDst(RegDst), .Branch(Branch), .Jump(JumpCtrl), .ALUOp_1__0(ALUOp),
    .ExtensionControl(ExtensionControl));
  Adder #(.width(32)) adder_1 (.a(CurrentPC), .b(32'h4), .out(adder_1_out));  // open: cin, cout
  Multiplexer #(.select(1), .width(5), .disabled("Z"), .enable("false")) multiplexer_2 (
    .in0(Jump[20:16]), .in1(Immediate[15:11]), .out(WriteReg), .sel(RegDst));
  Multiplexer #(.select(1), .width(32), .disabled("Z"), .enable("false")) multiplexer_3 (
    .in0(ReadData2), .in1(EXT_23071005_extendedimmediate), .out(multiplexer_3_out), .sel(ALUSrc));
  Shifter #(.width(32), .shift("ll")) shifter_1 (
    .in(EXT_23071005_extendedimmediate), .\dist (5'b00010), .out(shifter_1_out));
  ALU ALU_23071005 (.ALUOp(ALUOp), .OperandA(ReadData1), .OperandB(multiplexer_3_out), .Result(ALU_res), .Zero(Zero));
  Adder #(.width(32)) adder_2 (.a(shifter_1_out), .b(adder_1_out), .out(Branch_Target_Address));  // open: cin, cout
  Multiplexer #(.select(1), .width(32), .disabled("Z"), .enable("false")) multiplexer_4 (
    .in0(Branch_Target_Address), .in1({CurrentPC[31:28], Jump, Immediate, funct, 2'b00}), .out(S_J_addr),
    .sel(JumpCtrl));

  // Other names for the same wires on the sheet: Immediate[5:0] = funct; Jump[15:0] = {Immediate, funct};
  //   Jump_Target_Address[31:2] = {CurrentPC[31:28], Jump, Immediate, funct}; rd[4:0] = Immediate[15:11];
  //   rt[4:0] = Jump[20:16]; rs[4:0] = Jump[25:21]
endmodule

module IFU (
  input  PC_clk,
  input  PC_clr,
  input  [31:0] S_J_addr,
  input  command_sel,
  output [31:0] IM_data,
  output [31:0] CurrentPC
);

  wire [31:0] adder_1_out, multiplexer_1_out;

  Register #(.width(32), .trigger("rising"), .Select("low")) PC (
    .D(multiplexer_1_out), .en(1'b1), .Q(CurrentPC), .clk(PC_clk), .clr(PC_clr));
  Adder #(.width(32)) adder_1 (.a(CurrentPC), .b(32'h4), .out(adder_1_out));  // open: cin, cout
  Multiplexer #(.select(1), .width(32), .disabled("Z"), .enable("false")) multiplexer_1 (
    .in0(adder_1_out), .in1(S_J_addr), .out(multiplexer_1_out), .sel(command_sel));
  ROM #(.addrWidth(8), .dataWidth(8), .Select("low")) rom_1 (.addr(CurrentPC[9:2]), .data(IM_data[31:24]));
  ROM #(.addrWidth(8), .dataWidth(8), .Select("low")) rom_2 (.addr(CurrentPC[9:2]), .data(IM_data[23:16]));
  ROM #(.addrWidth(8), .dataWidth(8), .Select("low")) rom_3 (.addr(CurrentPC[9:2]), .data(IM_data[15:8]));
  ROM #(.addrWidth(8), .dataWidth(8), .Select("low")) rom_4 (.addr(CurrentPC[9:2]), .data(IM_data[7:0]));

  // Notes on the sheet:
  //   contents of rom_1 (hex, n*v repeats v):
  //   34 34 0 0 1 ac 8c 11 3c 8 34 3c 8
  //   contents of rom_2 (hex, n*v repeats v):
  //   3 6 66 66 2a 9 a 2a b 10 b 9 10
  //   contents of rom_3 (hex, n*v repeats v):
  //   0 0 40 48 4*0 cd 0 ef 45
  //   contents of rom_4 (hex, n*v repeats v):
  //   93 ae 21 23 21 10 10 2 cd d ef 67 7
endmodule

module GPR (
  input  [4:0] ReadReg1,
  input  [4:0] ReadReg2,
  input  clk,
  input  clr,
  input  [31:0] D,
  input  RegWrite,
  input  [4:0] WriteReg,
  output [31:0] ReadData1,
  output [31:0] ReadData2
);

  wire and_1_out, and_2_out, and_3_out, and_4_out, and_5_out, and_6_out, and_7_out, and_8_out, and_9_out,
       and_10_out, and_11_out, and_12_out, and_13_out, and_14_out, and_15_out, and_16_out, and_17_out,
       and_18_out, and_19_out, and_20_out, and_21_out, and_22_out, and_23_out, and_24_out, and_25_out,
       and_26_out, and_27_out, and_28_out, and_29_out, and_30_out, and_31_out, decoder_1_out1,
       decoder_1_out2, decoder_1_out3, decoder_1_out4, decoder_1_out5, decoder_1_out6, decoder_1_out7,
       decoder_1_out8, decoder_1_out9, decoder_1_out10, decoder_1_out11, decoder_1_out12, decoder_1_out13,
       decoder_1_out14, decoder_1_out15, decoder_1_out16, decoder_1_out17, decoder_1_out18, decoder_1_out19,
       decoder_1_out20, decoder_1_out21, decoder_1_out22, decoder_1_out23, decoder_1_out24, decoder_1_out25,
       decoder_1_out26, decoder_1_out27, decoder_1_out28, decoder_1_out29, decoder_1_out30, decoder_1_out31;
  wire [31:0] register_1_q, register_2_q, register_3_q, register_4_q, register_5_q, register_6_q,
       register_7_q, register_8_q, register_9_q, register_10_q, register_11_q, register_12_q, register_13_q,
       register_14_q, register_15_q, register_16_q, register_17_q, register_18_q, register_19_q,
       register_20_q, register_21_q, register_22_q, register_23_q, register_24_q, register_25_q,
       register_26_q, register_27_q, register_28_q, register_29_q, register_30_q, register_31_q,
       register_32_q;

  Decoder #(.select(5), .tristate("false"), .disabled("Z"), .enable("true")) decoder_1 (
    .out1(decoder_1_out1), .out2(decoder_1_out2), .out3(decoder_1_out3), .out4(decoder_1_out4),
    .out5(decoder_1_out5), .out6(decoder_1_out6), .out7(decoder_1_out7), .out8(decoder_1_out8),
    .out9(decoder_1_out9), .out10(decoder_1_out10), .out11(decoder_1_out11), .out12(decoder_1_out12),
    .out13(decoder_1_out13), .out14(decoder_1_out14), .out15(decoder_1_out15), .out16(decoder_1_out16),
    .out17(decoder_1_out17), .out18(decoder_1_out18), .out19(decoder_1_out19), .out20(decoder_1_out20),
    .out21(decoder_1_out21), .out22(decoder_1_out22), .out23(decoder_1_out23), .out24(decoder_1_out24),
    .out25(decoder_1_out25), .out26(decoder_1_out26), .out27(decoder_1_out27), .out28(decoder_1_out28),
    .out29(decoder_1_out29), .out30(decoder_1_out30), .out31(decoder_1_out31), .sel(WriteReg), .en(RegWrite));  // open: out0
  and and_1 (and_1_out, RegWrite, decoder_1_out1);
  and and_2 (and_2_out, RegWrite, decoder_1_out2);
  and and_3 (and_3_out, RegWrite, decoder_1_out3);
  and and_4 (and_4_out, RegWrite, decoder_1_out4);
  and and_5 (and_5_out, RegWrite, decoder_1_out5);
  and and_6 (and_6_out, RegWrite, decoder_1_out6);
  and and_7 (and_7_out, RegWrite, decoder_1_out7);
  Register #(.width(32), .trigger("rising"), .Select("low")) register_1 (
    .Q(register_1_q), .clk(clk), .clr(clr));  // open: D, en
  Register #(.width(32), .trigger("rising"), .Select("low")) register_2 (
    .D(D), .en(and_1_out), .Q(register_2_q), .clk(clk), .clr(clr));
  Register #(.width(32), .trigger("rising"), .Select("low")) register_3 (
    .D(D), .en(and_2_out), .Q(register_3_q), .clk(clk), .clr(clr));
  Register #(.width(32), .trigger("rising"), .Select("low")) register_4 (
    .D(D), .en(and_3_out), .Q(register_4_q), .clk(clk), .clr(clr));
  Register #(.width(32), .trigger("rising"), .Select("low")) register_5 (
    .D(D), .en(and_4_out), .Q(register_5_q), .clk(clk), .clr(clr));
  Register #(.width(32), .trigger("rising"), .Select("low")) register_6 (
    .D(D), .en(and_5_out), .Q(register_6_q), .clk(clk), .clr(clr));
  Register #(.width(32), .trigger("rising"), .Select("low")) register_7 (
    .D(D), .en(and_6_out), .Q(register_7_q), .clk(clk), .clr(clr));
  Register #(.width(32), .trigger("rising"), .Select("low")) register_8 (
    .D(D), .en(and_7_out), .Q(register_8_q), .clk(clk), .clr(clr));
  and and_8 (and_8_out, RegWrite, decoder_1_out8);
  and and_9 (and_9_out, RegWrite, decoder_1_out9);
  and and_10 (and_10_out, RegWrite, decoder_1_out10);
  and and_11 (and_11_out, RegWrite, decoder_1_out11);
  and and_12 (and_12_out, RegWrite, decoder_1_out12);
  and and_13 (and_13_out, RegWrite, decoder_1_out13);
  and and_14 (and_14_out, RegWrite, decoder_1_out14);
  and and_15 (and_15_out, RegWrite, decoder_1_out15);
  Register #(.width(32), .trigger("rising"), .Select("low")) register_9 (
    .D(D), .en(and_8_out), .Q(register_9_q), .clk(clk), .clr(clr));
  Register #(.width(32), .trigger("rising"), .Select("low")) register_10 (
    .D(D), .en(and_9_out), .Q(register_10_q), .clk(clk), .clr(clr));
  Register #(.width(32), .trigger("rising"), .Select("low")) register_11 (
    .D(D), .en(and_10_out), .Q(register_11_q), .clk(clk), .clr(clr));
  Register #(.width(32), .trigger("rising"), .Select("low")) register_12 (
    .D(D), .en(and_11_out), .Q(register_12_q), .clk(clk), .clr(clr));
  Register #(.width(32), .trigger("rising"), .Select("low")) register_13 (
    .D(D), .en(and_12_out), .Q(register_13_q), .clk(clk), .clr(clr));
  Register #(.width(32), .trigger("rising"), .Select("low")) register_14 (
    .D(D), .en(and_13_out), .Q(register_14_q), .clk(clk), .clr(clr));
  Register #(.width(32), .trigger("rising"), .Select("low")) register_15 (
    .D(D), .en(and_14_out), .Q(register_15_q), .clk(clk), .clr(clr));
  Register #(.width(32), .trigger("rising"), .Select("low")) register_16 (
    .D(D), .en(and_15_out), .Q(register_16_q), .clk(clk), .clr(clr));
  and and_16 (and_16_out, RegWrite, decoder_1_out16);
  and and_17 (and_17_out, RegWrite, decoder_1_out17);
  and and_18 (and_18_out, RegWrite, decoder_1_out18);
  and and_19 (and_19_out, RegWrite, decoder_1_out19);
  and and_20 (and_20_out, RegWrite, decoder_1_out20);
  and and_21 (and_21_out, RegWrite, decoder_1_out21);
  and and_22 (and_22_out, RegWrite, decoder_1_out22);
  and and_23 (and_23_out, RegWrite, decoder_1_out23);
  Register #(.width(32), .trigger("rising"), .Select("low")) register_17 (
    .D(D), .en(and_16_out), .Q(register_17_q), .clk(clk), .clr(clr));
  Register #(.width(32), .trigger("rising"), .Select("low")) register_18 (
    .D(D), .en(and_17_out), .Q(register_18_q), .clk(clk), .clr(clr));
  Register #(.width(32), .trigger("rising"), .Select("low")) register_19 (
    .D(D), .en(and_18_out), .Q(register_19_q), .clk(clk), .clr(clr));
  Register #(.width(32), .trigger("rising"), .Select("low")) register_20 (
    .D(D), .en(and_19_out), .Q(register_20_q), .clk(clk), .clr(clr));
  Register #(.width(32), .trigger("rising"), .Select("low")) register_21 (
    .D(D), .en(and_20_out), .Q(register_21_q), .clk(clk), .clr(clr));
  Register #(.width(32), .trigger("rising"), .Select("low")) register_22 (
    .D(D), .en(and_21_out), .Q(register_22_q), .clk(clk), .clr(clr));
  Register #(.width(32), .trigger("rising"), .Select("low")) register_23 (
    .D(D), .en(and_22_out), .Q(register_23_q), .clk(clk), .clr(clr));
  Register #(.width(32), .trigger("rising"), .Select("low")) register_24 (
    .D(D), .en(and_23_out), .Q(register_24_q), .clk(clk), .clr(clr));
  and and_24 (and_24_out, RegWrite, decoder_1_out24);
  and and_25 (and_25_out, RegWrite, decoder_1_out25);
  and and_26 (and_26_out, RegWrite, decoder_1_out26);
  and and_27 (and_27_out, RegWrite, decoder_1_out27);
  and and_28 (and_28_out, RegWrite, decoder_1_out28);
  and and_29 (and_29_out, RegWrite, decoder_1_out29);
  and and_30 (and_30_out, RegWrite, decoder_1_out30);
  and and_31 (and_31_out, RegWrite, decoder_1_out31);
  Register #(.width(32), .trigger("rising"), .Select("low")) register_25 (
    .D(D), .en(and_24_out), .Q(register_25_q), .clk(clk), .clr(clr));
  Register #(.width(32), .trigger("rising"), .Select("low")) register_26 (
    .D(D), .en(and_25_out), .Q(register_26_q), .clk(clk), .clr(clr));
  Register #(.width(32), .trigger("rising"), .Select("low")) register_27 (
    .D(D), .en(and_26_out), .Q(register_27_q), .clk(clk), .clr(clr));
  Register #(.width(32), .trigger("rising"), .Select("low")) register_28 (
    .D(D), .en(and_27_out), .Q(register_28_q), .clk(clk), .clr(clr));
  Register #(.width(32), .trigger("rising"), .Select("low")) register_29 (
    .D(D), .en(and_28_out), .Q(register_29_q), .clk(clk), .clr(clr));
  Register #(.width(32), .trigger("rising"), .Select("low")) register_30 (
    .D(D), .en(and_29_out), .Q(register_30_q), .clk(clk), .clr(clr));
  Register #(.width(32), .trigger("rising"), .Select("low")) register_31 (
    .D(D), .en(and_30_out), .Q(register_31_q), .clk(clk), .clr(clr));
  Register #(.width(32), .trigger("rising"), .Select("low")) register_32 (
    .D(D), .en(and_31_out), .Q(register_32_q), .clk(clk), .clr(clr));
  Multiplexer #(.select(5), .width(32), .disabled("Z"), .enable("false")) multiplexer_1 (
    .in0(register_1_q), .in1(register_2_q), .in2(register_3_q), .in3(register_4_q), .in4(register_5_q),
    .in5(register_6_q), .in6(register_7_q), .in7(register_8_q), .in8(register_9_q), .in9(register_10_q),
    .in10(register_11_q), .in11(register_12_q), .in12(register_13_q), .in13(register_14_q),
    .in14(register_15_q), .in15(register_16_q), .in16(register_17_q), .in17(register_18_q),
    .in18(register_19_q), .in19(register_20_q), .in20(register_21_q), .in21(register_22_q),
    .in22(register_23_q), .in23(register_24_q), .in24(register_25_q), .in25(register_26_q),
    .in26(register_27_q), .in27(register_28_q), .in28(register_29_q), .in29(register_30_q),
    .in30(register_31_q), .in31(register_32_q), .out(ReadData1), .sel(ReadReg1));
  Multiplexer #(.select(5), .width(32), .disabled("Z"), .enable("false")) multiplexer_2 (
    .in0(register_1_q), .in1(register_2_q), .in2(register_3_q), .in3(register_4_q), .in4(register_5_q),
    .in5(register_6_q), .in6(register_7_q), .in7(register_8_q), .in8(register_9_q), .in9(register_10_q),
    .in10(register_11_q), .in11(register_12_q), .in12(register_13_q), .in13(register_14_q),
    .in14(register_15_q), .in15(register_16_q), .in16(register_17_q), .in17(register_18_q),
    .in18(register_19_q), .in19(register_20_q), .in20(register_21_q), .in21(register_22_q),
    .in22(register_23_q), .in23(register_24_q), .in24(register_25_q), .in25(register_26_q),
    .in26(register_27_q), .in27(register_28_q), .in28(register_29_q), .in29(register_30_q),
    .in30(register_31_q), .in31(register_32_q), .out(ReadData2), .sel(ReadReg2));

  // Other names for the same wires on the sheet: reg_clk = clk; reg_clr = clr; reg_data[31:0] = D
endmodule

module ALU (
  input  [1:0] ALUOp,
  input  [31:0] OperandA,
  input  [31:0] OperandB,
  output [31:0] Result,
  output Zero
);

  wire [31:0] adder_1_out, or_1_out, subtractor_1_out;

  Adder #(.width(32)) adder_1 (.a(OperandA), .b(OperandB), .out(adder_1_out));  // open: cin, cout
  Subtractor #(.width(32)) subtractor_1 (.a(OperandA), .b(OperandB), .out(subtractor_1_out));  // open: bin, bout
  assign or_1_out = OperandA | OperandB;  // OR_Gate or_1, 32 bits wide
  Multiplexer #(.select(2), .width(32), .disabled("Z"), .enable("false")) multiplexer_1 (
    .in0(adder_1_out), .in1(subtractor_1_out), .in2(or_1_out), .out(Result), .sel(ALUOp));  // open: in3
  nor nor_1 (Zero, Result[0], Result[1], Result[2], Result[3], Result[4], Result[5], Result[6], Result[7], Result[8], Result[9], Result[10], Result[11], Result[12], Result[13], Result[14], Result[15], Result[17], Result[18], Result[19], Result[20], Result[21], Result[22], Result[23], Result[24], Result[25], Result[26], Result[27], Result[28], Result[29], Result[30], Result[31], Result[16]);
endmodule

module EXT (
  input  [15:0] Immediate16,
  input  [1:0] ExtensionControl,
  output [31:0] ExtendedImmediate
);

  wire [31:0] bit_extender_1_out, bit_extender_2_out;

  assign bit_extender_1_out = {{16{1'b0}}, Immediate16};  // Bit_Extender bit_extender_1
  assign bit_extender_2_out = {{16{Immediate16[15]}}, Immediate16};  // Bit_Extender bit_extender_2
  Multiplexer #(.select(2), .width(32), .disabled("Z"), .enable("false")) multiplexer_1 (
    .in0(bit_extender_1_out), .in1(bit_extender_2_out), .in2({Immediate16, {16{1'b0}}}),
    .out(ExtendedImmediate), .sel(ExtensionControl));  // open: in3

  // Notes on the sheet:
  //   高0扩展
  //   高符扩展
  //   低0扩展
endmodule

module DM (
  input  [31:0] Address,
  input  [31:0] WriteData,
  input  MemWrite,
  input  DM_clk,
  input  DM_reset,
  output [31:0] ReadData
);

  RAM #(.addrWidth(8), .dataWidth(8), .bus("separate"), .Select("low")) ram_1 (
    .addr(Address[9:2]), .din(WriteData[7:0]), .data(ReadData[7:0]), .str(MemWrite), .clk(DM_clk),
    .clr(DM_reset));  // open: sel, ld
  RAM #(.addrWidth(8), .dataWidth(8), .bus("separate"), .Select("low")) ram_2 (
    .addr(Address[9:2]), .din(WriteData[15:8]), .data(ReadData[15:8]), .str(MemWrite), .clk(DM_clk),
    .clr(DM_reset));  // open: sel, ld
  RAM #(.addrWidth(8), .dataWidth(8), .bus("separate"), .Select("low")) ram_3 (
    .addr(Address[9:2]), .din(WriteData[23:16]), .data(ReadData[23:16]), .str(MemWrite), .clk(DM_clk),
    .clr(DM_reset));  // open: sel, ld
  RAM #(.addrWidth(8), .dataWidth(8), .bus("separate"), .Select("low")) ram_4 (
    .addr(Address[9:2]), .din(WriteData[31:24]), .data(ReadData[31:24]), .str(MemWrite), .clk(DM_clk),
    .clr(DM_reset));  // open: sel, ld
endmodule

module Controller (
  input  [5:0] OpCode_31__26,
  input  [5:0] Funct_5__0,
  output RegWrite,
  output MemWrite,
  output ALUSrc,
  output MemtoReg,
  output RegDst,
  output Branch,
  output Jump,
  output [1:0] ALUOp_1__0,
  output [1:0] ExtensionControl
);

  wire addu_out, not_1_out, not_2_out, not_3_out, not_4_out, not_5_out, not_6_out, not_7_out, not_8_out,
       not_9_out, not_10_out, subu_out;

  not not_1 (not_1_out, OpCode_31__26[5]);
  not not_2 (not_2_out, OpCode_31__26[4]);
  not not_3 (not_3_out, OpCode_31__26[3]);
  not not_4 (not_4_out, OpCode_31__26[2]);
  not not_5 (not_5_out, OpCode_31__26[1]);
  not not_6 (not_6_out, OpCode_31__26[0]);
  not not_7 (not_7_out, Funct_5__0[4]);
  and ori (ALUOp_1__0[1], not_1_out, not_2_out, OpCode_31__26[3], OpCode_31__26[2], not_5_out, OpCode_31__26[0]);
  and lw (MemtoReg, OpCode_31__26[5], not_2_out, not_3_out, not_4_out, OpCode_31__26[1], OpCode_31__26[0]);
  and sw (MemWrite, OpCode_31__26[5], not_2_out, OpCode_31__26[3], not_4_out, OpCode_31__26[1], OpCode_31__26[0]);
  and beq (Branch, not_1_out, not_2_out, not_3_out, OpCode_31__26[2], not_5_out, not_6_out);
  and lui (ExtensionControl[1], not_1_out, not_2_out, OpCode_31__26[3], OpCode_31__26[2], OpCode_31__26[1], OpCode_31__26[0]);
  and u_jump (Jump, not_1_out, not_2_out, not_3_out, not_4_out, OpCode_31__26[1], not_6_out);
  not not_8 (not_8_out, Funct_5__0[3]);
  not not_9 (not_9_out, Funct_5__0[2]);
  not not_10 (not_10_out, Funct_5__0[1]);
  and addu (addu_out, not_1_out, not_2_out, not_3_out, not_4_out, not_5_out, not_6_out, Funct_5__0[5], not_7_out, not_8_out, not_9_out, not_10_out, Funct_5__0[0]);
  and subu (subu_out, not_1_out, not_2_out, not_3_out, not_4_out, not_5_out, not_6_out, Funct_5__0[5], not_7_out, not_8_out, not_9_out, Funct_5__0[1], Funct_5__0[0]);
  or or_1 (RegDst, addu_out, subu_out);
  or or_2 (RegWrite, addu_out, subu_out, ALUOp_1__0[1], MemtoReg, ExtensionControl[1]);
  or or_3 (ALUSrc, ALUOp_1__0[1], MemtoReg, ExtensionControl[1], MemWrite);
  or or_4 (ALUOp_1__0[0], subu_out, Branch);
  or or_5 (ExtensionControl[0], MemtoReg, MemWrite);
endmodule
